# Fritzing sketch Circuit (saved by Fritzing 1.0.5)

parts:
  A1 = S-350-60 Power Supply [part_number=S-350-60 package=THT]
  M1 = RioRand LM2596
  U1 = ESP32-38PinWide [part_number=ESP32-38PinWide]
  S1 = H-Bridge with L298N
  J1 = Camdenboss CTB0158-9 [part_number=CTB0158-9 package=THT]
  J2 = Camdenboss CTB0158-10 [part_number=CTB0158-10 package=THT]
  M1_2 = DC Motor [voltage_(max)=5V voltage_(min)=3V part_number=Vibrator]
  M3 = Dagu DGServo 9g (Pan and tilt) [part_number="Lock Servo"]
  M4 = Dagu DGServo 9g (Pan and tilt) [part_number="Port Servo"]
  M5 = RioRand LM2596
  J3 = Camdenboss CTB0158-9 [part_number=CTB0158-9 package=THT]
  J4 = Camdenboss CTB0158-9 [part_number=CTB0158-9 package=THT]
  M6 = Stepper Motor - Unipolar
  MD09B1 = A4988 Stepper Motor Driver Carrier

nets:
  N1: A1.+V1, A1.+V2, A1.+V3, M1.Pin_1, J1.pin1, J1.pin2, J1.pin3, J1.pin4, J1.pin5, J1.pin6, J1.pin7, J1.pin8, J1.pin9, M5.Pin_1
  N2: A1.-V1, A1.-V3, J2.pin1, J2.pin2, J2.pin3, J2.pin4, J2.pin5, J2.pin6, J2.pin7, J2.pin8, J2.pin9, J2.pin10
  N3: M1.Pin_2, J2.terminal_10
  N4: M1.Pin_3, U1.VIN
  N5: M1.Pin_4, U1.GPIO11
  N6: U1.GPIO33, M4.pulse
  N7: U1.GPIO17, M3.pulse
  N8: U1.GPIO18, S1.ENB
  N9: U1.GPIO19, S1.IN4
  N10: U1.GPIO21, S1.IN3
  N11: U1.GPIO22, MD09B1.DIR
  N12: U1.GPIO23, MD09B1.STEP
  N13: U1.GND, J2.terminal_8
  N14: S1.12V, J1.terminal_1
  N15: S1.GND, J2.terminal_1
  N16: S1.M2-01, M1_2.pin_2
  N17: S1.M2-02, M1_2.pin_1
  N18: J1.terminal_5, MD09B1.VMOT
  N19: J2.terminal_6, MD09B1.GROUND#141
  N20: J2.terminal_7, MD09B1.GROUND#147
  N21: J2.terminal_9, M5.Pin_2
  N22: M3.gnd, J4.terminal_2
  N23: M3.vcc, J3.terminal_8
  N24: M4.gnd, J4.terminal_1
  N25: M4.vcc, J3.terminal_9
  N26: M5.Pin_3, J3.pin1, J3.pin2, J3.pin3, J3.pin4, J3.pin5, J3.pin6, J3.pin7, J3.pin8, J3.pin9
  N27: M5.Pin_4, J4.pin1, J4.pin2, J4.pin3, J4.pin4, J4.pin5, J4.pin6, J4.pin7, J4.pin8, J4.pin9
  N28: J3.terminal_7, MD09B1.VDD
  N29: M6.A, MD09B1.OUT_2B
  N30: M6.C, MD09B1.OUT_2A
  N31: M6.B, MD09B1.OUT_1A
  N32: M6.D, MD09B1.OUT_1B
  N33: MD09B1.RESET, MD09B1.SLEEP

custom parts:
  S-350-60 Power Supply: 350W Stepper motor power supply. June 2024 clean up errors in the part.
  ESP32-38PinWide: Generic 38-Pin ESP32 with wide format (only access to one side of pins on a breadboard) based on Stephen Lilley's HiLetgo ESP-WROOM-32 ESP32 ESP-32S Development Board.
  H-Bridge with L298N: h-bridge
  Stepper Motor - Unipolar: A basic unipolar stepper motor
  A4988 Stepper Motor Driver Carrier: The Pololu stepper motor driver carrier for the A4988 motor driver integrated circuits. http://www.pololu.com/catalog/product/1182
